// Logisim project ZCS_4.circ as structural Verilog: 5 circuits, main circuit main
module main (
);

  wire undriven;
  wire [3:0] alu_1_out_0;

  RAM #(.addrWidth(4), .dataWidth(4)) ram_1 (
    .addr(alu_1_out_0), .clk(undriven), .din(alu_1_out_0));  // open: we, oe, dout
  REG_Y reg_y_1 (
    .IO_0(alu_1_out_0[0]), .IO_1(alu_1_out_0[1]), .IO_2(alu_1_out_0[2]), .IO_3(alu_1_out_0[3]), .CLK(undriven));  // open: WE, IR
  REG_X reg_x_1 (
    .IO_0(alu_1_out_0[0]), .IO_1(alu_1_out_0[1]), .IO_2(alu_1_out_0[2]), .IO_3(alu_1_out_0[3]), .CLK(undriven));  // open: WE, IR
  ALU alu_1 (
    .IN_Y_0(alu_1_out_0[0]), .IN_Y_1(alu_1_out_0[1]), .IN_Y_2(alu_1_out_0[2]), .IN_Y_3(alu_1_out_0[3]),
    .IN_X_0(alu_1_out_0[0]), .IN_X_1(alu_1_out_0[1]), .IN_X_2(alu_1_out_0[2]), .CLK(undriven),
    .IN_X_3(alu_1_out_0[3]), .OUT_0(alu_1_out_0[0]), .OUT_1(alu_1_out_0[1]), .OUT_2(alu_1_out_0[2]),
    .OUT_3(alu_1_out_0[3]));  // open: OE, C_OUT
endmodule

module REG_Y (
  input  IO_0,
  input  IO_1,
  input  IO_2,
  input  IO_3,
  input  WE,
  input  CLK,
  input  IR
);

  Register #(.width(4)) register_1 (
    .D({IO_3, IO_2, IO_1, IO_0}), .en(WE), .clk(CLK), .Q({IO_3, IO_2, IO_1, IO_0}), .clr(IR));
endmodule

module REG_X (
  input  IO_0,
  input  IO_1,
  input  IO_2,
  input  IO_3,
  input  WE,
  input  CLK,
  input  IR
);

  Register #(.width(4)) register_1 (
    .D({IO_3, IO_2, IO_1, IO_0}), .en(WE), .clk(CLK), .Q({IO_3, IO_2, IO_1, IO_0}), .clr(IR));
endmodule

module ALU (
  input  IN_Y_0,
  input  IN_Y_1,
  input  IN_Y_2,
  input  IN_Y_3,
  input  IN_X_0,
  input  IN_X_1,
  input  IN_X_2,
  input  CLK,
  input  IN_X_3,
  input  OE,
  output OUT_0,
  output OUT_1,
  output OUT_2,
  output OUT_3,
  output C_OUT
);

  wire not_1_out;
  wire [3:0] adder_1_out;

  Adder #(.width(4)) adder_1 (
    .a({IN_Y_3, IN_Y_2, IN_Y_1, IN_Y_0}), .b({IN_X_3, IN_X_2, IN_X_1, IN_X_0}), .out(adder_1_out),
    .cin(1'b0), .cout(C_OUT));
  Register #(.width(4)) register_1 (
    .D(adder_1_out), .en(1'b1), .clk(CLK), .Q({OUT_3, OUT_2, OUT_1, OUT_0}), .clr(not_1_out));
  not not_1 (not_1_out, OE);
endmodule

module PC (
);

  wire and_1_out, and_2_out, and_3_out, and_4_out, and_5_out, and_6_out, and_7_out, and_8_out, and_9_out,
       and_10_out, and_11_out, and_12_out, clock_1_out, controlled_inverter_1_out, controlled_inverter_2_out,
       controlled_inverter_3_out, controlled_inverter_4_out, j_k_ff_1_q, j_k_ff_1_qn, j_k_ff_2_q,
       j_k_ff_2_qn, j_k_ff_3_q, j_k_ff_3_qn, j_k_ff_4_qn, not_1_out, not_2_out, not_3_out, not_4_out,
       not_5_out, or_1_out, or_2_out, or_3_out, or_4_out, pull_resistor_5_node, switch_1_p2, switch_2_p1,
       switch_3_p1, switch_5_p1;
  wire [3:0] pull_resistor_4_node, register_1_q;

  Clock clock_1 (.out(clock_1_out));
  and and_1 (and_1_out, 1'b1, ~pull_resistor_5_node);  // AND_Gate
  and and_2 (and_2_out, pull_resistor_5_node, pull_resistor_4_node[3]);
  or or_1 (or_1_out, and_1_out, and_2_out);
  and and_3 (and_3_out, 1'b1, ~pull_resistor_5_node);  // AND_Gate
  or or_2 (or_2_out, and_3_out, and_4_out);
  and and_4 (and_4_out, pull_resistor_5_node, pull_resistor_4_node[2]);
  and and_5 (and_5_out, 1'b1, ~pull_resistor_5_node);  // AND_Gate
  or or_3 (or_3_out, and_5_out, and_6_out);
  and and_6 (and_6_out, pull_resistor_5_node, pull_resistor_4_node[1]);
  and and_7 (and_7_out, 1'b1, ~pull_resistor_5_node);  // AND_Gate
  and and_8 (and_8_out, pull_resistor_5_node, pull_resistor_4_node[0]);
  or or_4 (or_4_out, and_7_out, and_8_out);
  and and_9 (and_9_out, pull_resistor_5_node, or_4_out);
  and and_10 (and_10_out, pull_resistor_5_node, or_3_out);
  and and_11 (and_11_out, pull_resistor_5_node, or_2_out);
  and and_12 (and_12_out, pull_resistor_5_node, or_1_out);
  J_K_Flip_Flop j_k_ff_1 (
    .J(or_4_out), .K(controlled_inverter_1_out), .clk(clock_1_out), .Q(j_k_ff_1_q), .Qn(j_k_ff_1_qn));  // open: preset, reset
  not not_1 (not_1_out, pull_resistor_5_node);
  assign controlled_inverter_1_out = pull_resistor_5_node ? ~and_9_out : 1'bz;  // Controlled_Inverter controlled_inverter_1
  assign controlled_inverter_1_out = not_1_out ? or_4_out : 1'bz;  // Controlled_Buffer controlled_buffer_1
  J_K_Flip_Flop j_k_ff_2 (
    .J(or_3_out), .K(controlled_inverter_2_out), .clk(j_k_ff_1_q), .Q(j_k_ff_2_q), .Qn(j_k_ff_2_qn));  // open: preset, reset
  not not_2 (not_2_out, pull_resistor_5_node);
  assign controlled_inverter_2_out = pull_resistor_5_node ? ~and_10_out : 1'bz;  // Controlled_Inverter controlled_inverter_2
  assign controlled_inverter_2_out = not_2_out ? or_3_out : 1'bz;  // Controlled_Buffer controlled_buffer_2
  J_K_Flip_Flop j_k_ff_3 (
    .J(or_2_out), .K(controlled_inverter_3_out), .clk(j_k_ff_2_q), .Q(j_k_ff_3_q), .Qn(j_k_ff_3_qn));  // open: preset, reset
  not not_3 (not_3_out, pull_resistor_5_node);
  assign controlled_inverter_3_out = pull_resistor_5_node ? ~and_11_out : 1'bz;  // Controlled_Inverter controlled_inverter_3
  assign controlled_inverter_3_out = not_3_out ? or_2_out : 1'bz;  // Controlled_Buffer controlled_buffer_3
  J_K_Flip_Flop j_k_ff_4 (
    .J(or_1_out), .K(controlled_inverter_4_out), .clk(j_k_ff_3_q), .Qn(j_k_ff_4_qn));  // open: Q, preset, reset
  not not_4 (not_4_out, pull_resistor_5_node);
  assign controlled_inverter_4_out = pull_resistor_5_node ? ~and_12_out : 1'bz;  // Controlled_Inverter controlled_inverter_4
  assign controlled_inverter_4_out = not_4_out ? or_1_out : 1'bz;  // Controlled_Buffer controlled_buffer_4
  Pull_Resistor pull_resistor_1 (.node(pull_resistor_4_node[3]));
  Pull_Resistor pull_resistor_2 (.node(pull_resistor_4_node[2]));
  Pull_Resistor pull_resistor_3 (.node(pull_resistor_4_node[1]));
  Pull_Resistor pull_resistor_4 (.node(pull_resistor_4_node[0]));
  // Switch switch_1: pin names not known; wires that end beside it: 1'b1, switch_1_p2, 1'b1
  // Switch switch_2: pin names not known; wires that end beside it: switch_2_p1, 1'b1
  // Switch switch_3: pin names not known; wires that end beside it: switch_3_p1, 1'b1
  assign pull_resistor_4_node[0] = pull_resistor_5_node ? switch_1_p2 : 1'bz;  // Controlled_Buffer controlled_buffer_5
  assign pull_resistor_4_node[1] = pull_resistor_5_node ? switch_2_p1 : 1'bz;  // Controlled_Buffer controlled_buffer_6
  assign pull_resistor_4_node[2] = pull_resistor_5_node ? switch_3_p1 : 1'bz;  // Controlled_Buffer controlled_buffer_7
  assign pull_resistor_4_node[0] = not_5_out ? j_k_ff_1_qn : 1'bz;  // Controlled_Buffer controlled_buffer_8
  assign pull_resistor_4_node[1] = not_5_out ? j_k_ff_2_qn : 1'bz;  // Controlled_Buffer controlled_buffer_9
  Pull_Resistor pull_resistor_5 (.node(pull_resistor_5_node));
  // Switch switch_4: pin names not known; wires that end beside it: 1'b1, pull_resistor_5_node
  // Switch switch_5: pin names not known; wires that end beside it: switch_5_p1
  assign pull_resistor_4_node[3] = pull_resistor_5_node ? switch_5_p1 : 1'bz;  // Controlled_Buffer controlled_buffer_10
  assign pull_resistor_4_node[2] = not_5_out ? j_k_ff_3_qn : 1'bz;  // Controlled_Buffer controlled_buffer_11
  assign pull_resistor_4_node[3] = not_5_out ? j_k_ff_4_qn : 1'bz;  // Controlled_Buffer controlled_buffer_12
  not not_5 (not_5_out, pull_resistor_5_node);
  Register #(.width(4)) register_1 (
    .D(pull_resistor_4_node), .en(1'b1), .clk(clock_1_out), .Q(register_1_q), .clr(1'b0));
  LED led_1 (.in(register_1_q[1]));
  LED led_2 (.in(register_1_q[2]));
  LED led_3 (.in(register_1_q[0]));
  LED led_4 (.in(register_1_q[3]));
endmodule
